// Logisim project Exemplo 1 - S=(A.B).(C+D+E).circ as structural Verilog: 1 circuit, main circuit main
module main (
  input  A,
  input  B,
  input  C,
  input  D,
  input  E
);

  wire S1_out, S2_out, S3_out;

  and S1 (S1_out, A, B);
  or S2 (S2_out, C, D, E);
  and S3 (S3_out, S1_out, S2_out);
  LED S (.in(S3_out));

  // Notes on the sheet:
  //   S = (A*B)*(C+D+E)
endmodule
