// Logisim project Como cada uma funciona.circ as structural Verilog: 1 circuit, main circuit main
module main (
  input  A,
  input  B,
  input  C,
  input  A_2,
  input  B_2,
  input  C_2,
  input  A_3,
  input  A_4,
  input  B_3,
  input  B_4,
  input  C_3,
  input  C_4,
  input  A_5,
  input  B_5,
  input  C_5,
  input  A_6,
  input  B_6
);

  wire and_1_out, and_2_out, nand_1_out, nor_1_out, or_1_out, xor_1_out;

  and and_1 (and_1_out, A, B, C);
  or or_1 (or_1_out, A_2, B_2, C_2);
  LED led_1 (.in(and_1_out));
  LED led_2 (.in(or_1_out));
  nand nand_1 (nand_1_out, A_3, B_3, C_3);
  LED led_3 (.in(nand_1_out));
  LED led_4 (.in(nor_1_out));
  nor nor_1 (nor_1_out, A_5, B_5, C_5);
  xor xor_1 (xor_1_out, A_6, B_6);
  LED led_5 (.in(xor_1_out));
  and and_2 (and_2_out, ~A_4, B_4, C_4);  // AND_Gate
  LED led_6 (.in(and_2_out));

  // Notes on the sheet:
  //   S=!(A.B.C)
  //   S=!(A+B+C)
  //   S=ABC
  //   S=A+B+C
  //   Essa é a XOR, ela funciona tipo a OR, só que quando der 1+1 ela vai resultar em 0
  //   S
  //   S
  //   OBS: O ! faz o papel do barrado
  //   S
  //   S
  //   S
  //   S=!A.B.C
  //   S
endmodule
