// Logisim project Circuito da Prova.circ as structural Verilog: 1 circuit, main circuit main
module main (
  input  A,
  input  B,
  input  C,
  input  D,
  input  E,
  output S
);

  wire and_1_out, and_2_out, nand_1_out, nor_1_out, not_1_out, or_1_out;

  or or_1 (or_1_out, C, D);
  not not_1 (not_1_out, and_1_out);
  and and_1 (and_1_out, A, B);
  nand nand_1 (nand_1_out, or_1_out, E);
  and and_2 (and_2_out, nand_1_out, D);
  nor nor_1 (nor_1_out, not_1_out, nand_1_out);
  xor xor_1 (S, nor_1_out, and_2_out);
endmodule
